# Fritzing sketch BME280_lcd (saved by Fritzing 0.9.4)
breadboards: 1

parts:
  Mod1 = Raspberry Pi Pico
  BMP280_Breakout1 = BMP280 Breakout Board [part_number=BMP280]
  Componente1 = LCD1602-I2C

nets:
  N1: Mod1.pin_1, BMP280_Breakout1.SDA, Componente1.SDA
  N2: Mod1.pin_2, BMP280_Breakout1.SCL, Componente1.SCL
  GND: Mod1.pin_3, Mod1.pin_8, Mod1.pin_13, Mod1.pin_18, Mod1.pin_23, Mod1.pin_28, Mod1.pin_33, Mod1.pin_38, BMP280_Breakout1.GND, Componente1.GND
  VCC: Mod1.pin_37, BMP280_Breakout1.VCC, Componente1.VCC

custom parts:
  Raspberry Pi Pico: Raspberry Pi Pico. Based around the RP2040 microcontroller the Pico is a low cost microcontroller device bringing Raspberry Pi quality, cost, and easy of use to the microcontroller space. Jan 2021, Split part in to two versions: tht (this one) and SMD. This one will drill holes for a .1 in header in pcb to allow plugging in the module as well as providing pads to solder the module to the top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
  BMP280 Breakout Board: This is a breakout board for the Bosch Sensortec BMP280, "an absolute barometric pressure sensor especially designed for mobile applications." The operation range is 300 to 1100 hPa. Supply voltage is 1.2 to 3.6V. Operating temperature range is -40 to +85 °C.
  LCD1602-I2C: A standard character display, usually with 2x16 characters. Comes in many colors with LCM1602 IIC attached.
